# Fritzing sketch LuceIngresso (saved by Fritzing 0.3.14b)
breadboards: 1

parts:
  Arduino2009 = Arduino
  SENSORIR = Infrared Proximity Sensor
  SENSORLUM = Photocell (LDR) [package=THT]  # not connected
  R2 = Resistor [resistance=220 package=THT]
  S1 = Pushbutton [package="[THT]"]
  R3 = Resistor [resistance=220 package=THT]
  ULN2003A1 = ULN2003A
  Power_plug1 = Power plug
  RGB_Strip1 = Generic female header - 4 pins [form="♀ (female)"]

nets:
  GND: Arduino2009.GND, SENSORIR.GND, ULN2003A1.connector7, Power_plug1.GND
  N1: Arduino2009.D12, R3.Pin_0
  N2: Arduino2009.D6, ULN2003A1.connector0
  N3: Arduino2009.D5, ULN2003A1.connector1
  N4: Arduino2009.D3, ULN2003A1.connector2
  +5V: Arduino2009.+5V, SENSORIR.Vcc, S1.Pin_1, S1.Pin_2
  N5: Arduino2009.A0, R2.Pin_0
  N6: Arduino2009.A5, SENSORIR.Vout
  N7: S1.Pin_3, S1.Pin_4, R3.Pin_1
  N8: ULN2003A1.connector13, RGB_Strip1.connector3
  N9: ULN2003A1.connector14, RGB_Strip1.connector2
  N10: ULN2003A1.connector15, RGB_Strip1.connector1
  N11: Power_plug1.VCC, RGB_Strip1.connector0

notes:
  Sensore di prossimità Sharp GP2Y0A21YK
  Arduino \Source code: http://github.com/amedeos/LuceInIngresso/blob/master/LuceIngresso/LuceIngresso.pde
  Alimentatore 12V 500mA
  Seven Darlington Array
  ULN2003A
